// Logisim project 16bit4.circ as structural Verilog: 3 circuits, main circuit main
module main (
  input  [1:0] Operation,
  input  Cin,
  input  [15:0] Operand_B,
  input  [15:0] Operand_A,
  input  Binvert,
  output ZeroFlag,
  output [15:0] Result,
  output OverFlow,
  output Cout
);

  _16BitALU_L_2 u_16bitalu_l_2_1 (
    .Cin(Cin), .OperandB(Operand_B), .Operand_A(Operand_A), .Binvert(Binvert), .OperationBit(Operation),
    .ZeroFlag(ZeroFlag), .OverFlow(OverFlow), .Cout(Cout), .out_6(Result));
endmodule

// !6BitALU
module _16BitALU_L_2 (
  input  Cin,
  input  [15:0] OperandB,
  input  [15:0] Operand_A,
  input  Binvert,
  input  [1:0] OperationBit,
  output [15:0] out_6,
  output ZeroFlag,
  output OverFlow,
  output Cout
);

  wire alu_1_bit_1_carry, alu_1_bit_2_carry, alu_1_bit_3_carry, alu_1_bit_4_carry, alu_1_bit_5_carry,
       alu_1_bit_6_carry, alu_1_bit_7_carry, alu_1_bit_8_carry, alu_1_bit_9_carry, alu_1_bit_10_carry,
       alu_1_bit_11_carry, alu_1_bit_12_carry, alu_1_bit_13_carry, alu_1_bit_14_carry, alu_1_bit_15_carry;

  ALU_1_Bit alu_1_bit_1 (
    .Operation(OperationBit), .Binvert(Binvert), .Result(out_6[0]), .Carry(alu_1_bit_1_carry),
    .Operand_B(OperandB[0]), .Operand_A(Operand_A[0]), .CarryIn(Cin));
  ALU_1_Bit alu_1_bit_2 (
    .Operation(OperationBit), .Binvert(Binvert), .Result(out_6[1]), .Carry(alu_1_bit_2_carry),
    .Operand_B(OperandB[1]), .Operand_A(Operand_A[1]), .CarryIn(alu_1_bit_1_carry));
  ALU_1_Bit alu_1_bit_3 (
    .Operation(OperationBit), .Binvert(Binvert), .Result(out_6[2]), .Carry(alu_1_bit_3_carry),
    .Operand_B(OperandB[2]), .Operand_A(Operand_A[2]), .CarryIn(alu_1_bit_2_carry));
  ALU_1_Bit alu_1_bit_4 (
    .Operation(OperationBit), .Binvert(Binvert), .Result(out_6[3]), .Carry(alu_1_bit_4_carry),
    .Operand_B(OperandB[3]), .Operand_A(Operand_A[3]), .CarryIn(alu_1_bit_3_carry));
  ALU_1_Bit alu_1_bit_5 (
    .Operation(OperationBit), .Binvert(Binvert), .Result(out_6[4]), .Carry(alu_1_bit_5_carry),
    .Operand_B(OperandB[4]), .Operand_A(Operand_A[4]), .CarryIn(alu_1_bit_4_carry));
  ALU_1_Bit alu_1_bit_6 (
    .Operation(OperationBit), .Binvert(Binvert), .Result(out_6[5]), .Carry(alu_1_bit_6_carry),
    .Operand_B(OperandB[5]), .Operand_A(Operand_A[5]), .CarryIn(alu_1_bit_5_carry));
  ALU_1_Bit alu_1_bit_7 (
    .Operation(OperationBit), .Binvert(Binvert), .Result(out_6[6]), .Carry(alu_1_bit_7_carry),
    .Operand_B(OperandB[6]), .Operand_A(Operand_A[6]), .CarryIn(alu_1_bit_6_carry));
  ALU_1_Bit alu_1_bit_8 (
    .Operation(OperationBit), .Binvert(Binvert), .Result(out_6[7]), .Carry(alu_1_bit_8_carry),
    .Operand_B(OperandB[7]), .Operand_A(Operand_A[7]), .CarryIn(alu_1_bit_7_carry));
  ALU_1_Bit alu_1_bit_9 (
    .Operation(OperationBit), .Binvert(Binvert), .Result(out_6[8]), .Carry(alu_1_bit_9_carry),
    .Operand_B(OperandB[8]), .Operand_A(Operand_A[8]), .CarryIn(alu_1_bit_8_carry));
  ALU_1_Bit alu_1_bit_10 (
    .Operation(OperationBit), .Binvert(Binvert), .Result(out_6[9]), .Carry(alu_1_bit_10_carry),
    .Operand_B(OperandB[9]), .Operand_A(Operand_A[9]), .CarryIn(alu_1_bit_9_carry));
  ALU_1_Bit alu_1_bit_11 (
    .Operation(OperationBit), .Binvert(Binvert), .Result(out_6[10]), .Carry(alu_1_bit_11_carry),
    .Operand_B(OperandB[10]), .Operand_A(Operand_A[10]), .CarryIn(alu_1_bit_10_carry));
  ALU_1_Bit alu_1_bit_12 (
    .Operation(OperationBit), .Binvert(Binvert), .Result(out_6[11]), .Carry(alu_1_bit_12_carry),
    .Operand_B(OperandB[11]), .Operand_A(Operand_A[11]), .CarryIn(alu_1_bit_11_carry));
  ALU_1_Bit alu_1_bit_13 (
    .Operation(OperationBit), .Binvert(Binvert), .Result(out_6[12]), .Carry(alu_1_bit_13_carry),
    .Operand_B(OperandB[12]), .Operand_A(Operand_A[12]), .CarryIn(alu_1_bit_12_carry));
  ALU_1_Bit alu_1_bit_14 (
    .Operation(OperationBit), .Binvert(Binvert), .Result(out_6[13]), .Carry(alu_1_bit_14_carry),
    .Operand_B(OperandB[13]), .Operand_A(Operand_A[13]), .CarryIn(alu_1_bit_13_carry));
  ALU_1_Bit alu_1_bit_15 (
    .Operation(OperationBit), .Binvert(Binvert), .Result(out_6[14]), .Carry(alu_1_bit_15_carry),
    .Operand_B(OperandB[14]), .Operand_A(Operand_A[14]), .CarryIn(alu_1_bit_14_carry));
  ALU_1_Bit alu_1_bit_16 (
    .Operation(OperationBit), .Binvert(Binvert), .Result(out_6[15]), .Carry(Cout), .Operand_B(OperandB[15]),
    .Operand_A(Operand_A[15]), .CarryIn(alu_1_bit_15_carry));
  xor xor_1 (OverFlow, alu_1_bit_15_carry, Cout);
  nor nor_1 (ZeroFlag, out_6[0], out_6[1], out_6[2], out_6[3], out_6[4], out_6[5], out_6[6], out_6[7], out_6[8], out_6[9], out_6[10], out_6[11], out_6[12], out_6[13], out_6[14], out_6[15]);
endmodule

// 1 Bit ALU
module ALU_1_Bit (
  input  CarryIn,
  input  Operand_B,
  input  Operand_A,
  input  [1:0] Operation,
  input  Binvert,
  output Result,
  output Carry
);

  wire adder_1_out, and_1_out, multiplexer_1_out, not_1_out, or_1_out;

  not not_1 (not_1_out, Operand_B);
  and and_1 (and_1_out, Operand_A, Operand_B);
  or or_1 (or_1_out, Operand_A, Operand_B);
  Multiplexer multiplexer_1 (.in0(Operand_B), .in1(not_1_out), .out(multiplexer_1_out), .sel(Binvert));  // open: en
  Adder #(.width(1)) adder_1 (.a(Operand_A), .b(multiplexer_1_out), .out(adder_1_out), .cin(CarryIn), .cout(Carry));
  Multiplexer #(.select(2)) multiplexer_2 (
    .in0(and_1_out), .in1(or_1_out), .in2(adder_1_out), .out(Result), .sel(Operation));  // open: in3, en
endmodule
