// Logisim project SingleCircuitDataPath.circ as structural Verilog
// !6BitALU
module _16BitALU_L_2 (
  input  Cin,
  input  [15:0] OperandB,
  input  [15:0] Operand_A,
  input  Binvert,
  input  [1:0] OperationBit,
  output [15:0] Result,
  output ZeroFlag,
  output OverFlow,
  output Cout
);

  wire alu_1_bit_1_carry, alu_1_bit_2_carry, alu_1_bit_3_carry, alu_1_bit_4_carry, alu_1_bit_5_carry,
       alu_1_bit_6_carry, alu_1_bit_7_carry, alu_1_bit_8_carry, alu_1_bit_9_carry, alu_1_bit_10_carry,
       alu_1_bit_11_carry, alu_1_bit_12_carry, alu_1_bit_13_carry, alu_1_bit_14_carry, alu_1_bit_15_carry;

  ALU_1_Bit alu_1_bit_1 (
    .Operation(OperationBit), .Binvert(Binvert), .Result(Result[0]), .Carry(alu_1_bit_1_carry),
    .Operand_B(OperandB[0]), .Operand_A(Operand_A[0]), .CarryIn(Cin));
  ALU_1_Bit alu_1_bit_2 (
    .Operation(OperationBit), .Binvert(Binvert), .Result(Result[1]), .Carry(alu_1_bit_2_carry),
    .Operand_B(OperandB[1]), .Operand_A(Operand_A[1]), .CarryIn(alu_1_bit_1_carry));
  ALU_1_Bit alu_1_bit_3 (
    .Operation(OperationBit), .Binvert(Binvert), .Result(Result[2]), .Carry(alu_1_bit_3_carry),
    .Operand_B(OperandB[2]), .Operand_A(Operand_A[2]), .CarryIn(alu_1_bit_2_carry));
  ALU_1_Bit alu_1_bit_4 (
    .Operation(OperationBit), .Binvert(Binvert), .Result(Result[3]), .Carry(alu_1_bit_4_carry),
    .Operand_B(OperandB[3]), .Operand_A(Operand_A[3]), .CarryIn(alu_1_bit_3_carry));
  ALU_1_Bit alu_1_bit_5 (
    .Operation(OperationBit), .Binvert(Binvert), .Result(Result[4]), .Carry(alu_1_bit_5_carry),
    .Operand_B(OperandB[4]), .Operand_A(Operand_A[4]), .CarryIn(alu_1_bit_4_carry));
  ALU_1_Bit alu_1_bit_6 (
    .Operation(OperationBit), .Binvert(Binvert), .Result(Result[5]), .Carry(alu_1_bit_6_carry),
    .Operand_B(OperandB[5]), .Operand_A(Operand_A[5]), .CarryIn(alu_1_bit_5_carry));
  ALU_1_Bit alu_1_bit_7 (
    .Operation(OperationBit), .Binvert(Binvert), .Result(Result[6]), .Carry(alu_1_bit_7_carry),
    .Operand_B(OperandB[6]), .Operand_A(Operand_A[6]), .CarryIn(alu_1_bit_6_carry));
  ALU_1_Bit alu_1_bit_8 (
    .Operation(OperationBit), .Binvert(Binvert), .Result(Result[7]), .Carry(alu_1_bit_8_carry),
    .Operand_B(OperandB[7]), .Operand_A(Operand_A[7]), .CarryIn(alu_1_bit_7_carry));
  ALU_1_Bit alu_1_bit_9 (
    .Operation(OperationBit), .Binvert(Binvert), .Result(Result[8]), .Carry(alu_1_bit_9_carry),
    .Operand_B(OperandB[8]), .Operand_A(Operand_A[8]), .CarryIn(alu_1_bit_8_carry));
  ALU_1_Bit alu_1_bit_10 (
    .Operation(OperationBit), .Binvert(Binvert), .Result(Result[9]), .Carry(alu_1_bit_10_carry),
    .Operand_B(OperandB[9]), .Operand_A(Operand_A[9]), .CarryIn(alu_1_bit_9_carry));
  ALU_1_Bit alu_1_bit_11 (
    .Operation(OperationBit), .Binvert(Binvert), .Result(Result[10]), .Carry(alu_1_bit_11_carry),
    .Operand_B(OperandB[10]), .Operand_A(Operand_A[10]), .CarryIn(alu_1_bit_10_carry));
  ALU_1_Bit alu_1_bit_12 (
    .Operation(OperationBit), .Binvert(Binvert), .Result(Result[11]), .Carry(alu_1_bit_12_carry),
    .Operand_B(OperandB[11]), .Operand_A(Operand_A[11]), .CarryIn(alu_1_bit_11_carry));
  ALU_1_Bit alu_1_bit_13 (
    .Operation(OperationBit), .Binvert(Binvert), .Result(Result[12]), .Carry(alu_1_bit_13_carry),
    .Operand_B(OperandB[12]), .Operand_A(Operand_A[12]), .CarryIn(alu_1_bit_12_carry));
  ALU_1_Bit alu_1_bit_14 (
    .Operation(OperationBit), .Binvert(Binvert), .Result(Result[13]), .Carry(alu_1_bit_14_carry),
    .Operand_B(OperandB[13]), .Operand_A(Operand_A[13]), .CarryIn(alu_1_bit_13_carry));
  ALU_1_Bit alu_1_bit_15 (
    .Operation(OperationBit), .Binvert(Binvert), .Result(Result[14]), .Carry(alu_1_bit_15_carry),
    .Operand_B(OperandB[14]), .Operand_A(Operand_A[14]), .CarryIn(alu_1_bit_14_carry));
  ALU_1_Bit alu_1_bit_16 (
    .Operation(OperationBit), .Binvert(Binvert), .Result(Result[15]), .Carry(Cout), .Operand_B(OperandB[15]),
    .Operand_A(Operand_A[15]), .CarryIn(alu_1_bit_15_carry));
  xor xor_1 (OverFlow, alu_1_bit_15_carry, Cout);
  nor nor_1 (ZeroFlag, Result[0], Result[1], Result[2], Result[3], Result[4], Result[5], Result[6], Result[7], Result[8], Result[9], Result[10], Result[11], Result[12], Result[13], Result[14], Result[15]);
endmodule

// 1 Bit ALU
module ALU_1_Bit (
  input  CarryIn,
  input  Operand_B,
  input  Operand_A,
  input  [1:0] Operation,
  input  Binvert,
  output Result,
  output Carry
);

  wire adder_1_out, and_1_out, multiplexer_1_out, not_1_out, or_1_out;

  not not_1 (not_1_out, Operand_B);
  and and_1 (and_1_out, Operand_A, Operand_B);
  or or_1 (or_1_out, Operand_A, Operand_B);
  Multiplexer multiplexer_1 (.in0(Operand_B), .in1(not_1_out), .out(multiplexer_1_out), .sel(Binvert));  // open: en
  Adder #(.width(1)) adder_1 (.a(Operand_A), .b(multiplexer_1_out), .out(adder_1_out), .cin(CarryIn), .cout(Carry));
  Multiplexer #(.select(2)) multiplexer_2 (
    .in0(and_1_out), .in1(or_1_out), .in2(adder_1_out), .out(Result), .sel(Operation));  // open: in3, en
endmodule

// 0001
module SingleCircuitDataPath (
  input  MemToReg,
  input  Binvert,
  input  RegDst,
  input  RegWrite,
  input  AluSrc,
  input  MemWrite_prime,
  input  MemRead,
  output out_8,
  output out_9,
  output out_10
);

  wire clock_1_out;
  wire [3:0] multiplexer_1_out;
  wire [15:0] bit_extender_1_out, multiplexer_2_out, multiplexer_3_out, n16bit_register_file_1_out_7,
       n16bit_register_file_1_out_8, n16bitalu_l_2_1_result, ram_1_data;
  wire [19:0] adder_1_out, ProgramCounter_q, rom_1_data, undriven;

  Clock clock_1 (.out(clock_1_out));
  Counter #(.width(20), .max('hfffff)) ProgramCounter (
    .D(adder_1_out), .Q(ProgramCounter_q), .clk(clock_1_out), .clr(Binvert));  // open: load, count, carry
  Adder #(.width(20)) adder_1 (.a(undriven), .b(ProgramCounter_q), .out(adder_1_out));  // open: cin, cout
  ROM #(.addrWidth(20), .dataWidth(20)) rom_1 (.addr(ProgramCounter_q), .data(rom_1_data));  // open: sel
  Multiplexer #(.width(4), .enable("false")) multiplexer_1 (
    .in0(rom_1_data[11:8]), .in1(rom_1_data[7:4]), .out(multiplexer_1_out), .sel(RegDst));
  assign bit_extender_1_out = {{8{rom_1_data[7]}}, rom_1_data[7:0]};  // Bit_Extender bit_extender_1
  _16bit_Register_File u_16bit_register_file_1 (
    .DAta_In(multiplexer_3_out), .out_7(n16bit_register_file_1_out_7), .out_8(n16bit_register_file_1_out_8),
    .Data_Address__rd(multiplexer_1_out), .Register_Weite(RegWrite), .Clock(clock_1_out),
    .Read_Address_1_rs(rom_1_data[15:12]), .Read_Address_2_rt(rom_1_data[11:8]));
  Multiplexer #(.width(16)) multiplexer_2 (
    .in0(n16bit_register_file_1_out_8), .in1(bit_extender_1_out), .out(multiplexer_2_out), .sel(AluSrc));  // open: en
  _16BitALU_L_2 u_16bitalu_l_2_1 (
    .Cin(rom_1_data[18]), .OperandB(n16bit_register_file_1_out_7), .Operand_A(multiplexer_2_out),
    .OperationBit(rom_1_data[17:16]), .ZeroFlag(out_10), .OverFlow(out_9), .Cout(out_8),
    .Result(n16bitalu_l_2_1_result));  // open: Binvert
  Multiplexer #(.width(16), .enable("false")) multiplexer_3 (
    .in0(n16bitalu_l_2_1_result), .in1(ram_1_data), .out(multiplexer_3_out), .sel(MemToReg));
  RAM #(.addrWidth(16), .dataWidth(16), .bus("separate")) ram_1 (
    .addr(n16bitalu_l_2_1_result), .din(n16bit_register_file_1_out_8), .data(ram_1_data),
    .str(MemWrite_prime), .clk(clock_1_out), .ld(MemRead));  // open: sel, clr
endmodule
